// Logisim project washing_pipeline.circ as structural Verilog: 23 circuits, main circuit Main
module Mux2Bit (
  input  [1:0] A,
  input  [1:0] B,
  input  S,
  output [1:0] Y
);

  wire [1:0] and_1_out, and_2_out, not_1_out;

  assign not_1_out = ~{2{S}};  // NOT_Gate not_1, 2 bits wide
  assign and_1_out = A & not_1_out;  // AND_Gate and_1, 2 bits wide
  assign and_2_out = B & {2{S}};  // AND_Gate and_2, 2 bits wide
  assign Y = and_1_out | and_2_out;  // OR_Gate or_1, 2 bits wide
endmodule

module Mux3Bit (
  input  [2:0] A,
  input  [2:0] B,
  input  S,
  output [2:0] Y
);

  wire [2:0] and_1_out, and_2_out, not_1_out;

  assign not_1_out = ~{3{S}};  // NOT_Gate not_1, 3 bits wide
  assign and_1_out = A & not_1_out;  // AND_Gate and_1, 3 bits wide
  assign and_2_out = B & {3{S}};  // AND_Gate and_2, 3 bits wide
  assign Y = and_1_out | and_2_out;  // OR_Gate or_1, 3 bits wide
endmodule

module Mux4Bit (
  input  [3:0] A,
  input  [3:0] B,
  input  S,
  output [3:0] Y
);

  wire [3:0] and_1_out, and_2_out, not_1_out;

  assign not_1_out = ~{4{S}};  // NOT_Gate not_1, 4 bits wide
  assign and_1_out = A & not_1_out;  // AND_Gate and_1, 4 bits wide
  assign and_2_out = B & {4{S}};  // AND_Gate and_2, 4 bits wide
  assign Y = and_1_out | and_2_out;  // OR_Gate or_1, 4 bits wide
endmodule

module Mux7Bit (
  input  [6:0] A,
  input  [6:0] B,
  input  S,
  output [6:0] Y
);

  wire [6:0] and_1_out, and_2_out, not_1_out;

  assign not_1_out = ~{7{S}};  // NOT_Gate not_1, 7 bits wide
  assign and_1_out = A & not_1_out;  // AND_Gate and_1, 7 bits wide
  assign and_2_out = B & {7{S}};  // AND_Gate and_2, 7 bits wide
  assign Y = and_1_out | and_2_out;  // OR_Gate or_1, 7 bits wide
endmodule

module Mux8Bit (
  input  [7:0] A,
  input  [7:0] B,
  input  S,
  output [7:0] Y
);

  wire [7:0] and_1_out, and_2_out, not_1_out;

  assign not_1_out = ~{8{S}};  // NOT_Gate not_1, 8 bits wide
  assign and_1_out = A & not_1_out;  // AND_Gate and_1, 8 bits wide
  assign and_2_out = B & {8{S}};  // AND_Gate and_2, 8 bits wide
  assign Y = and_1_out | and_2_out;  // OR_Gate or_1, 8 bits wide
endmodule

module Mux16Bit (
  input  [15:0] A,
  input  [15:0] B,
  input  S,
  output [15:0] Y
);

  wire [15:0] and_1_out, and_2_out, not_1_out;

  assign not_1_out = ~{16{S}};  // NOT_Gate not_1, 16 bits wide
  assign and_1_out = A & not_1_out;  // AND_Gate and_1, 16 bits wide
  assign and_2_out = B & {16{S}};  // AND_Gate and_2, 16 bits wide
  assign Y = and_1_out | and_2_out;  // OR_Gate or_1, 16 bits wide
endmodule

module Equal2Bit (
  input  [1:0] A,
  input  [1:0] B,
  output EQ
);

  wire or_1_out;
  wire [1:0] xor_1_out;

  // XOR_Gate xor_1 has open pins: out=xor_1_out
  or or_1 (or_1_out, xor_1_out[0], xor_1_out[1]);
  not not_1 (EQ, or_1_out);
endmodule

module Equal3Bit (
  input  [2:0] A,
  input  [2:0] B,
  output EQ
);

  wire or_1_out, or_2_out;
  wire [2:0] xor_1_out;

  // XOR_Gate xor_1 has open pins: out=xor_1_out
  or or_1 (or_1_out, xor_1_out[0], xor_1_out[1]);
  or or_2 (or_2_out, or_1_out, xor_1_out[2]);
  not not_1 (EQ, or_2_out);
endmodule

module Equal4Bit (
  input  [3:0] A,
  input  [3:0] B,
  output EQ
);

  wire or_1_out, or_2_out, or_3_out;
  wire [3:0] xor_1_out;

  // XOR_Gate xor_1 has open pins: out=xor_1_out
  or or_1 (or_1_out, xor_1_out[0], xor_1_out[1]);
  or or_2 (or_2_out, or_1_out, xor_1_out[2]);
  or or_3 (or_3_out, or_2_out, xor_1_out[3]);
  not not_1 (EQ, or_3_out);
endmodule

module Equal7Bit (
  input  [6:0] A,
  input  [6:0] B,
  output EQ
);

  wire or_1_out, or_2_out, or_3_out, or_4_out, or_5_out, or_6_out;
  wire [6:0] xor_1_out;

  // XOR_Gate xor_1 has open pins: out=xor_1_out
  or or_1 (or_1_out, xor_1_out[0], xor_1_out[1]);
  or or_2 (or_2_out, or_1_out, xor_1_out[2]);
  or or_3 (or_3_out, or_2_out, xor_1_out[3]);
  or or_4 (or_4_out, or_3_out, xor_1_out[4]);
  or or_5 (or_5_out, or_4_out, xor_1_out[5]);
  or or_6 (or_6_out, or_5_out, xor_1_out[6]);
  not not_1 (EQ, or_6_out);
endmodule

module Equal8Bit (
  input  [7:0] A,
  input  [7:0] B,
  output EQ
);

  wire or_1_out, or_2_out, or_3_out, or_4_out, or_5_out, or_6_out, or_7_out;
  wire [7:0] xor_1_out;

  // XOR_Gate xor_1 has open pins: out=xor_1_out
  or or_1 (or_1_out, xor_1_out[0], xor_1_out[1]);
  or or_2 (or_2_out, or_1_out, xor_1_out[2]);
  or or_3 (or_3_out, or_2_out, xor_1_out[3]);
  or or_4 (or_4_out, or_3_out, xor_1_out[4]);
  or or_5 (or_5_out, or_4_out, xor_1_out[5]);
  or or_6 (or_6_out, or_5_out, xor_1_out[6]);
  or or_7 (or_7_out, or_6_out, xor_1_out[7]);
  not not_1 (EQ, or_7_out);
endmodule

module Equal16Bit (
  input  [15:0] A,
  input  [15:0] B,
  output EQ
);

  wire or_1_out, or_2_out, or_3_out, or_4_out, or_5_out, or_6_out, or_7_out, or_8_out, or_9_out, or_10_out,
       or_11_out, or_12_out, or_13_out, or_14_out, or_15_out;
  wire [15:0] xor_1_out;

  // XOR_Gate xor_1 has open pins: out=xor_1_out
  or or_1 (or_1_out, xor_1_out[0], xor_1_out[1]);
  or or_2 (or_2_out, or_1_out, xor_1_out[2]);
  or or_3 (or_3_out, or_2_out, xor_1_out[3]);
  or or_4 (or_4_out, or_3_out, xor_1_out[4]);
  or or_5 (or_5_out, or_4_out, xor_1_out[5]);
  or or_6 (or_6_out, or_5_out, xor_1_out[6]);
  or or_7 (or_7_out, or_6_out, xor_1_out[7]);
  or or_8 (or_8_out, or_7_out, xor_1_out[8]);
  or or_9 (or_9_out, or_8_out, xor_1_out[9]);
  or or_10 (or_10_out, or_9_out, xor_1_out[10]);
  or or_11 (or_11_out, or_10_out, xor_1_out[11]);
  or or_12 (or_12_out, or_11_out, xor_1_out[12]);
  or or_13 (or_13_out, or_12_out, xor_1_out[13]);
  or or_14 (or_14_out, or_13_out, xor_1_out[14]);
  or or_15 (or_15_out, or_14_out, xor_1_out[15]);
  not not_1 (EQ, or_15_out);
endmodule

module ByteAdder (
  input  [7:0] A,
  input  [7:0] B,
  input  CIN,
  output [7:0] SUM,
  output COUT
);

  wire and_1_out, and_2_out, and_3_out, and_4_out, and_5_out, and_6_out, and_7_out, and_8_out, and_9_out,
       and_10_out, and_11_out, and_12_out, and_13_out, and_14_out, and_15_out, and_16_out, or_1_out,
       or_2_out, or_3_out, or_4_out, or_5_out, or_6_out, or_7_out, xor_1_out, xor_2_out, xor_3_out,
       xor_4_out, xor_5_out, xor_6_out, xor_7_out, xor_8_out;

  // XOR_Gate xor_1 has open pins: out=xor_1_out
  and and_1 (and_1_out, A[0], B[0]);
  // XOR_Gate xor_2 has open pins: out=xor_2_out
  and and_2 (and_2_out, A[1], B[1]);
  // XOR_Gate xor_3 has open pins: out=xor_3_out
  and and_3 (and_3_out, A[2], B[2]);
  // XOR_Gate xor_4 has open pins: out=xor_4_out
  and and_4 (and_4_out, A[3], B[3]);
  // XOR_Gate xor_5 has open pins: out=xor_5_out
  and and_5 (and_5_out, A[4], B[4]);
  // XOR_Gate xor_6 has open pins: out=xor_6_out
  and and_6 (and_6_out, A[5], B[5]);
  // XOR_Gate xor_7 has open pins: out=xor_7_out
  and and_7 (and_7_out, A[6], B[6]);
  // XOR_Gate xor_8 has open pins: out=xor_8_out
  and and_8 (and_8_out, A[7], B[7]);
  // XOR_Gate xor_9 has open pins: out=SUM[0]
  and and_9 (and_9_out, xor_1_out, CIN);
  or or_1 (or_1_out, and_1_out, and_9_out);
  // XOR_Gate xor_10 has open pins: out=SUM[1]
  and and_10 (and_10_out, xor_2_out, or_1_out);
  or or_2 (or_2_out, and_2_out, and_10_out);
  // XOR_Gate xor_11 has open pins: out=SUM[2]
  and and_11 (and_11_out, xor_3_out, or_2_out);
  or or_3 (or_3_out, and_3_out, and_11_out);
  // XOR_Gate xor_12 has open pins: out=SUM[3]
  and and_12 (and_12_out, xor_4_out, or_3_out);
  or or_4 (or_4_out, and_4_out, and_12_out);
  // XOR_Gate xor_13 has open pins: out=SUM[4]
  and and_13 (and_13_out, xor_5_out, or_4_out);
  or or_5 (or_5_out, and_5_out, and_13_out);
  // XOR_Gate xor_14 has open pins: out=SUM[5]
  and and_14 (and_14_out, xor_6_out, or_5_out);
  or or_6 (or_6_out, and_6_out, and_14_out);
  // XOR_Gate xor_15 has open pins: out=SUM[6]
  and and_15 (and_15_out, xor_7_out, or_6_out);
  or or_7 (or_7_out, and_7_out, and_15_out);
  // XOR_Gate xor_16 has open pins: out=SUM[7]
  and and_16 (and_16_out, xor_8_out, or_7_out);
  or or_8 (COUT, and_8_out, and_16_out);
endmodule

module InstructionDecoder (
  input  [15:0] IR,
  output [2:0] RD,
  output [7:0] IMM,
  output LD,
  output HT,
  output [3:0] OP,
  output US,
  output RW,
  output JP,
  output ST,
  output UD,
  output BN,
  output BZ,
  output [2:0] RS
);

  wire and_2_out, and_4_out, and_7_out, and_8_out, and_9_out, and_10_out, and_11_out, and_14_out,
       equal4bit_1_eq, equal4bit_2_eq, equal4bit_3_eq, equal4bit_4_eq, equal4bit_5_eq, equal4bit_6_eq,
       equal4bit_7_eq, equal4bit_8_eq, equal4bit_9_eq, equal4bit_10_eq, equal4bit_11_eq, equal4bit_12_eq,
       equal4bit_13_eq, equal4bit_14_eq, not_1_out, not_2_out, not_3_out, not_4_out, or_1_out, or_2_out,
       or_3_out, or_4_out, or_5_out, or_6_out, or_7_out, or_8_out, or_9_out, or_10_out, or_11_out, or_12_out,
       or_13_out, or_14_out, or_15_out, or_16_out, or_17_out, or_18_out, or_19_out, or_20_out, or_21_out,
       or_22_out, or_23_out, or_24_out, or_25_out, or_26_out, or_27_out, or_28_out, or_29_out, or_30_out,
       or_31_out, or_32_out, or_33_out, or_34_out, or_36_out, or_37_out, or_38_out, or_41_out, or_42_out,
       or_43_out, or_44_out, or_45_out, or_46_out, or_47_out, or_48_out, or_49_out, or_50_out, or_51_out,
       or_52_out;

  or or_1 (or_1_out, IR[0], IR[1]);
  not not_1 (not_1_out, IR[8]);
  or or_2 (or_2_out, IR[8], IR[9]);
  or or_3 (or_3_out, IR[0], IR[1]);
  Equal4Bit equal4bit_1 (.A(IR[15:12]), .B(4'b0111), .EQ(equal4bit_1_eq));
  or or_4 (or_4_out, or_3_out, IR[2]);
  Equal4Bit equal4bit_2 (.A(IR[15:12]), .B(4'b1000), .EQ(equal4bit_2_eq));
  Equal4Bit equal4bit_3 (.A(IR[15:12]), .B(4'b0000), .EQ(equal4bit_3_eq));
  Equal4Bit equal4bit_4 (.A(IR[15:12]), .B(4'b1001), .EQ(equal4bit_4_eq));
  Equal4Bit equal4bit_5 (.A(IR[15:12]), .B(4'b0001), .EQ(equal4bit_5_eq));
  Equal4Bit equal4bit_6 (.A(IR[15:12]), .B(4'b1010), .EQ(equal4bit_6_eq));
  Equal4Bit equal4bit_7 (.A(IR[15:12]), .B(4'b0010), .EQ(equal4bit_7_eq));
  Equal4Bit equal4bit_8 (.A(IR[15:12]), .B(4'b1011), .EQ(equal4bit_8_eq));
  Equal4Bit equal4bit_9 (.A(IR[15:12]), .B(4'b0011), .EQ(equal4bit_9_eq));
  Equal4Bit equal4bit_10 (.A(IR[15:12]), .B(4'b1100), .EQ(equal4bit_10_eq));
  Equal4Bit equal4bit_11 (.A(IR[15:12]), .B(4'b0100), .EQ(equal4bit_11_eq));
  or or_5 (or_5_out, or_1_out, IR[2]);
  Equal4Bit equal4bit_12 (.A(IR[15:12]), .B(4'b1101), .EQ(equal4bit_12_eq));
  Equal4Bit equal4bit_13 (.A(IR[15:12]), .B(4'b0101), .EQ(equal4bit_13_eq));
  Equal4Bit equal4bit_14 (.A(IR[15:12]), .B(4'b0110), .EQ(equal4bit_14_eq));
  or or_6 (or_6_out, or_2_out, IR[10]);
  or or_7 (or_7_out, or_6_out, IR[11]);
  or or_8 (or_8_out, or_4_out, IR[3]);
  or or_9 (or_9_out, or_5_out, IR[3]);
  and and_1 (BN, equal4bit_6_eq, not_1_out);
  and and_2 (and_2_out, equal4bit_2_eq, not_1_out);
  and and_3 (BZ, equal4bit_4_eq, not_1_out);
  and and_4 (and_4_out, equal4bit_5_eq, not_1_out);
  not not_2 (not_2_out, or_7_out);
  or or_10 (or_10_out, or_8_out, IR[4]);
  or or_11 (or_11_out, or_9_out, IR[4]);
  or or_12 (or_12_out, or_10_out, IR[5]);
  or or_13 (or_13_out, or_11_out, IR[5]);
  and and_5 (JP, equal4bit_8_eq, not_2_out);
  or or_14 (or_14_out, or_12_out, IR[6]);
  not not_3 (not_3_out, or_13_out);
  or or_15 (or_15_out, or_14_out, IR[7]);
  and and_6 (ST, equal4bit_1_eq, not_3_out);
  and and_7 (and_7_out, equal4bit_11_eq, not_3_out);
  and and_8 (and_8_out, equal4bit_7_eq, not_3_out);
  and and_9 (and_9_out, equal4bit_12_eq, not_3_out);
  and and_10 (and_10_out, equal4bit_9_eq, not_3_out);
  and and_11 (and_11_out, equal4bit_13_eq, not_3_out);
  and and_12 (LD, equal4bit_14_eq, not_3_out);
  or or_16 (or_16_out, or_15_out, IR[8]);
  or or_17 (or_17_out, and_10_out, and_7_out);
  or or_18 (or_18_out, and_8_out, and_10_out);
  or or_19 (or_19_out, and_4_out, and_8_out);
  or or_20 (or_20_out, or_16_out, IR[9]);
  or or_21 (or_21_out, or_18_out, and_7_out);
  or or_22 (or_22_out, or_17_out, and_11_out);
  or or_23 (or_23_out, or_19_out, and_10_out);
  or or_24 (or_24_out, or_20_out, IR[10]);
  or or_25 (or_25_out, or_22_out, ST);
  or or_26 (or_26_out, or_23_out, and_7_out);
  or or_27 (or_27_out, or_21_out, and_11_out);
  or or_28 (or_28_out, or_24_out, IR[11]);
  or or_29 (or_29_out, or_27_out, LD);
  or or_30 (or_30_out, or_25_out, and_2_out);
  or or_31 (or_31_out, or_26_out, and_11_out);
  not not_4 (not_4_out, or_28_out);
  or or_32 (or_32_out, or_29_out, ST);
  or or_33 (or_33_out, or_31_out, LD);
  or or_34 (or_34_out, or_30_out, BZ);
  and and_13 (HT, equal4bit_10_eq, not_4_out);
  and and_14 (and_14_out, equal4bit_3_eq, not_4_out);
  or or_35 (US, or_32_out, and_9_out);
  or or_36 (or_36_out, or_33_out, and_2_out);
  or or_37 (or_37_out, or_34_out, BN);
  or or_38 (or_38_out, and_14_out, and_4_out);
  or or_39 (RW, or_36_out, and_9_out);
  or or_40 (UD, or_37_out, and_9_out);
  or or_41 (or_41_out, or_38_out, and_8_out);
  or or_42 (or_42_out, or_41_out, and_10_out);
  or or_43 (or_43_out, or_42_out, and_7_out);
  or or_44 (or_44_out, or_43_out, and_11_out);
  or or_45 (or_45_out, or_44_out, LD);
  or or_46 (or_46_out, or_45_out, ST);
  or or_47 (or_47_out, or_46_out, and_2_out);
  or or_48 (or_48_out, or_47_out, BZ);
  or or_49 (or_49_out, or_48_out, BN);
  or or_50 (or_50_out, or_49_out, JP);
  or or_51 (or_51_out, or_50_out, HT);
  or or_52 (or_52_out, or_51_out, and_9_out);
  Mux4Bit mux4bit_1 (.A(4'b0000), .B(IR[15:12]), .S(or_52_out), .Y(OP));

  assign IMM = IR[7:0];
  assign RD = IR[11:9];
  assign RS = IR[8:6];
endmodule

module ALU (
  input  [7:0] A,
  input  [7:0] B,
  input  [7:0] IMM,
  input  [3:0] OP,
  output [7:0] RESULT
);

  wire equal4bit_2_eq, equal4bit_3_eq, equal4bit_4_eq, equal4bit_5_eq, equal4bit_6_eq, equal4bit_7_eq,
       equal4bit_9_eq, equal4bit_11_eq, equal4bit_12_eq, or_2_out, or_3_out;
  wire [0:0] byteadder_1_cout;
  wire [7:0] and_1_out, and_2_out, and_3_out, and_4_out, and_5_out, and_6_out, byteadder_1_sum, mux8bit_1_y,
       or_6_out, or_7_out, or_8_out, or_9_out, xor_1_out;
  wire [7:7] equal4bit_1_eq, equal4bit_8_eq, equal4bit_10_eq, or_1_out, or_4_out, or_5_out;

  assign and_1_out = A & B;  // AND_Gate and_1, 8 bits wide
  Equal4Bit equal4bit_1 (.A(OP), .B(4'b0001), .EQ(equal4bit_1_eq[7]));
  Equal4Bit equal4bit_2 (.A(OP), .B(4'b0010), .EQ(equal4bit_2_eq));
  Equal4Bit equal4bit_3 (.A(OP), .B(4'b0110), .EQ(equal4bit_3_eq));
  Equal4Bit equal4bit_4 (.A(OP), .B(4'b0111), .EQ(equal4bit_4_eq));
  Equal4Bit equal4bit_5 (.A(OP), .B(4'b0011), .EQ(equal4bit_5_eq));
  Equal4Bit equal4bit_6 (.A(OP), .B(4'b0100), .EQ(equal4bit_6_eq));
  Equal4Bit equal4bit_7 (.A(OP), .B(4'b0100), .EQ(equal4bit_7_eq));
  Equal4Bit equal4bit_8 (.A(OP), .B(4'b0101), .EQ(equal4bit_8_eq[7]));
  Equal4Bit equal4bit_9 (.A(OP), .B(4'b1101), .EQ(equal4bit_9_eq));
  Equal4Bit equal4bit_10 (.A(OP), .B(4'b1101), .EQ(equal4bit_10_eq[7]));
  Equal4Bit equal4bit_11 (.A(OP), .B(4'b1000), .EQ(equal4bit_11_eq));
  Equal4Bit equal4bit_12 (.A(OP), .B(4'b1000), .EQ(equal4bit_12_eq));
  or or_1 (or_1_out[7], equal4bit_6_eq, equal4bit_9_eq);
  or or_2 (or_2_out, equal4bit_2_eq, equal4bit_3_eq);
  Mux8Bit mux8bit_1 (.A(B), .B(IMM), .S(equal4bit_11_eq), .Y(mux8bit_1_y));
  or or_3 (or_3_out, equal4bit_5_eq, equal4bit_7_eq);
  assign and_2_out = IMM & {8{equal4bit_1_eq[7]}};  // AND_Gate and_2, 8 bits wide
  assign and_3_out = and_1_out & {8{equal4bit_8_eq[7]}};  // AND_Gate and_3, 8 bits wide
  or or_4 (or_4_out[7], or_3_out, equal4bit_12_eq);
  or or_5 (or_5_out[7], or_2_out, equal4bit_4_eq);
  assign or_6_out = {8{1'b0}} | and_2_out;  // OR_Gate or_6, 8 bits wide
  // XOR_Gate xor_1 has open pins: out=xor_1_out
  ByteAdder byteadder_1 (.A(A), .B(xor_1_out), .CIN(or_1_out[7]), .SUM(byteadder_1_sum), .COUT(byteadder_1_cout[0]));
  assign and_4_out = B & {8{or_5_out[7]}};  // AND_Gate and_4, 8 bits wide
  assign or_7_out = or_6_out | and_4_out;  // OR_Gate or_7, 8 bits wide
  assign and_5_out = byteadder_1_sum & {8{or_4_out[7]}};  // AND_Gate and_5, 8 bits wide
  assign and_6_out = {{7{1'b0}}, byteadder_1_cout[0]} & {8{equal4bit_10_eq[7]}};  // AND_Gate and_6, 8 bits wide
  assign or_8_out = or_7_out | and_5_out;  // OR_Gate or_8, 8 bits wide
  assign or_9_out = or_8_out | and_3_out;  // OR_Gate or_9, 8 bits wide
  assign RESULT = or_9_out | and_6_out;  // OR_Gate or_10, 8 bits wide
endmodule

module Forwarding (
  input  [7:0] RAW,
  input  [2:0] WB_RD,
  input  [2:0] SRC,
  input  WB_W,
  input  USED,
  input  [7:0] WB_DATA,
  input  [2:0] EM_RD,
  input  EM_W,
  input  EM_LD,
  input  [7:0] EM_DATA,
  output [1:0] SELECT,
  output [7:0] VALUE
);

  wire and_1_out, and_2_out, and_3_out, and_4_out, equal3bit_1_eq, equal3bit_2_eq, not_1_out, not_2_out;
  wire [7:0] mux8bit_1_y;

  Equal3Bit equal3bit_1 (.A(SRC), .B(WB_RD), .EQ(equal3bit_1_eq));
  and and_1 (and_1_out, USED, WB_W);
  Equal3Bit equal3bit_2 (.A(SRC), .B(EM_RD), .EQ(equal3bit_2_eq));
  and and_2 (and_2_out, USED, EM_W);
  not not_1 (not_1_out, EM_LD);
  and and_3 (and_3_out, and_1_out, equal3bit_1_eq);
  and and_4 (and_4_out, and_2_out, equal3bit_2_eq);
  not not_2 (not_2_out, and_4_out);
  and and_5 (SELECT[0], and_4_out, not_1_out);
  and and_6 (SELECT[1], and_3_out, not_2_out);
  Mux8Bit mux8bit_1 (.A(RAW), .B(WB_DATA), .S(SELECT[1]), .Y(mux8bit_1_y));
  Mux8Bit mux8bit_2 (.A(mux8bit_1_y), .B(EM_DATA), .S(SELECT[0]), .Y(VALUE));
endmodule

module RegisterBank (
  input  CLK,
  input  RESET,
  input  [2:0] WA,
  input  [7:0] WD,
  input  WE,
  input  [2:0] RA,
  input  [2:0] RB,
  output [7:0] B,
  output [7:0] A
);

  wire and_1_out, and_2_out, and_3_out, and_4_out, and_5_out, and_6_out, and_7_out, and_8_out, and_9_out,
       and_10_out, and_11_out, and_12_out, and_13_out, and_14_out, and_15_out, and_16_out, and_17_out,
       and_18_out, and_19_out, and_20_out, and_21_out, and_22_out, and_23_out, and_24_out, and_25_out,
       and_26_out, not_1_out, not_2_out, not_3_out, not_4_out, not_5_out, or_1_out, or_2_out, or_3_out,
       or_4_out;
  wire [2:0] xor_1_out, xor_2_out;
  wire [7:0] mux8bit_1_y, mux8bit_2_y, mux8bit_3_y, mux8bit_4_y, mux8bit_5_y, mux8bit_6_y, mux8bit_7_y,
       mux8bit_8_y, mux8bit_9_y, mux8bit_10_y, mux8bit_11_y, mux8bit_12_y, mux8bit_13_y, mux8bit_14_y,
       STATE_R0_q, STATE_R1_q, STATE_R2_q, STATE_R3_q, STATE_R4_q, STATE_R5_q, STATE_R6_q, STATE_R7_q;

  Register #(.width(8)) STATE_R0 (.D(WD), .en(and_21_out), .Q(STATE_R0_q), .clk(CLK), .clr(RESET));
  Register #(.width(8)) STATE_R1 (.D(WD), .en(and_19_out), .Q(STATE_R1_q), .clk(CLK), .clr(RESET));
  Register #(.width(8)) STATE_R2 (.D(WD), .en(and_22_out), .Q(STATE_R2_q), .clk(CLK), .clr(RESET));
  Register #(.width(8)) STATE_R3 (.D(WD), .en(and_20_out), .Q(STATE_R3_q), .clk(CLK), .clr(RESET));
  Register #(.width(8)) STATE_R4 (.D(WD), .en(and_23_out), .Q(STATE_R4_q), .clk(CLK), .clr(RESET));
  Register #(.width(8)) STATE_R5 (.D(WD), .en(and_15_out), .Q(STATE_R5_q), .clk(CLK), .clr(RESET));
  Register #(.width(8)) STATE_R6 (.D(WD), .en(and_24_out), .Q(STATE_R6_q), .clk(CLK), .clr(RESET));
  Register #(.width(8)) STATE_R7 (.D(WD), .en(and_16_out), .Q(STATE_R7_q), .clk(CLK), .clr(RESET));
  // XOR_Gate xor_1 has open pins: out=xor_1_out
  // XOR_Gate xor_2 has open pins: out=xor_2_out
  not not_1 (not_1_out, WA[0]);
  not not_2 (not_2_out, WA[1]);
  not not_3 (not_3_out, WA[2]);
  and and_1 (and_1_out, WE, WA[0]);
  and and_2 (and_2_out, WE, WA[0]);
  and and_3 (and_3_out, WE, WA[0]);
  and and_4 (and_4_out, WE, WA[0]);
  Mux8Bit mux8bit_1 (.A(STATE_R2_q), .B(STATE_R3_q), .S(RA[0]), .Y(mux8bit_1_y));
  Mux8Bit mux8bit_2 (.A(STATE_R2_q), .B(STATE_R3_q), .S(RB[0]), .Y(mux8bit_2_y));
  Mux8Bit mux8bit_3 (.A(STATE_R0_q), .B(STATE_R1_q), .S(RA[0]), .Y(mux8bit_3_y));
  Mux8Bit mux8bit_4 (.A(STATE_R0_q), .B(STATE_R1_q), .S(RB[0]), .Y(mux8bit_4_y));
  Mux8Bit mux8bit_5 (.A(STATE_R4_q), .B(STATE_R5_q), .S(RA[0]), .Y(mux8bit_5_y));
  Mux8Bit mux8bit_6 (.A(STATE_R4_q), .B(STATE_R5_q), .S(RB[0]), .Y(mux8bit_6_y));
  Mux8Bit mux8bit_7 (.A(STATE_R6_q), .B(STATE_R7_q), .S(RA[0]), .Y(mux8bit_7_y));
  Mux8Bit mux8bit_8 (.A(STATE_R6_q), .B(STATE_R7_q), .S(RB[0]), .Y(mux8bit_8_y));
  Mux8Bit mux8bit_9 (.A(mux8bit_3_y), .B(mux8bit_1_y), .S(RA[1]), .Y(mux8bit_9_y));
  and and_5 (and_5_out, WE, not_1_out);
  and and_6 (and_6_out, WE, not_1_out);
  and and_7 (and_7_out, WE, not_1_out);
  and and_8 (and_8_out, WE, not_1_out);
  and and_9 (and_9_out, and_1_out, not_2_out);
  and and_10 (and_10_out, and_2_out, WA[1]);
  Mux8Bit mux8bit_10 (.A(mux8bit_4_y), .B(mux8bit_2_y), .S(RB[1]), .Y(mux8bit_10_y));
  or or_1 (or_1_out, xor_1_out[0], xor_1_out[1]);
  Mux8Bit mux8bit_11 (.A(mux8bit_6_y), .B(mux8bit_8_y), .S(RB[1]), .Y(mux8bit_11_y));
  and and_11 (and_11_out, and_3_out, not_2_out);
  and and_12 (and_12_out, and_4_out, WA[1]);
  or or_2 (or_2_out, xor_2_out[0], xor_2_out[1]);
  Mux8Bit mux8bit_12 (.A(mux8bit_5_y), .B(mux8bit_7_y), .S(RA[1]), .Y(mux8bit_12_y));
  and and_13 (and_13_out, and_5_out, not_2_out);
  and and_14 (and_14_out, and_6_out, WA[1]);
  and and_15 (and_15_out, and_11_out, WA[2]);
  or or_3 (or_3_out, or_1_out, xor_1_out[2]);
  and and_16 (and_16_out, and_12_out, WA[2]);
  and and_17 (and_17_out, and_7_out, not_2_out);
  and and_18 (and_18_out, and_8_out, WA[1]);
  Mux8Bit mux8bit_13 (.A(mux8bit_9_y), .B(mux8bit_12_y), .S(RA[2]), .Y(mux8bit_13_y));
  and and_19 (and_19_out, and_9_out, not_3_out);
  Mux8Bit mux8bit_14 (.A(mux8bit_10_y), .B(mux8bit_11_y), .S(RB[2]), .Y(mux8bit_14_y));
  and and_20 (and_20_out, and_10_out, not_3_out);
  or or_4 (or_4_out, or_2_out, xor_2_out[2]);
  and and_21 (and_21_out, and_13_out, not_3_out);
  and and_22 (and_22_out, and_14_out, not_3_out);
  and and_23 (and_23_out, and_17_out, WA[2]);
  not not_4 (not_4_out, or_3_out);
  and and_24 (and_24_out, and_18_out, WA[2]);
  not not_5 (not_5_out, or_4_out);
  and and_25 (and_25_out, WE, not_4_out);
  and and_26 (and_26_out, WE, not_5_out);
  Mux8Bit mux8bit_15 (.A(mux8bit_14_y), .B(WD), .S(and_26_out), .Y(B));
  Mux8Bit mux8bit_16 (.A(mux8bit_13_y), .B(WD), .S(and_25_out), .Y(A));
endmodule

module Timer (
  input  CLK,
  input  RESET,
  input  [7:0] DATA,
  input  W_LIMIT,
  input  W_CTRL,
  output ENABLE,
  output [7:0] LIMIT,
  output MATCH,
  output [7:0] COUNT
);

  wire and_1_out, and_2_out, and_3_out, and_4_out, equal8bit_1_eq, equal8bit_2_eq, not_1_out, not_2_out,
       or_1_out, or_2_out;
  wire [7:0] byteadder_1_sum, mux8bit_1_y;

  Register #(.width(8)) STATE_COUNT (.D(mux8bit_1_y), .en(or_1_out), .Q(COUNT), .clk(CLK), .clr(RESET));
  Register #(.width(8)) STATE_LIMIT (.D(DATA), .en(W_LIMIT), .Q(LIMIT), .clk(CLK), .clr(RESET));
  Register #(.width(1)) STATE_ENABLE (.D(DATA[0]), .en(W_CTRL), .Q(ENABLE), .clk(CLK), .clr(RESET));
  Register #(.width(1)) STATE_MATCH (.D(and_4_out), .en(1'b1), .Q(MATCH), .clk(CLK), .clr(RESET));
  ByteAdder byteadder_1 (.A(COUNT), .B(8'h1), .CIN(1'b0), .SUM(byteadder_1_sum));  // open: COUT
  Equal8Bit equal8bit_1 (.A(LIMIT), .B({8{1'b0}}), .EQ(equal8bit_1_eq));
  and and_1 (and_1_out, W_CTRL, DATA[1]);
  Equal8Bit equal8bit_2 (.A(byteadder_1_sum), .B(LIMIT), .EQ(equal8bit_2_eq));
  not not_1 (not_1_out, equal8bit_1_eq);
  not not_2 (not_2_out, and_1_out);
  or or_1 (or_1_out, ENABLE, and_1_out);
  and and_2 (and_2_out, ENABLE, not_1_out);
  Mux8Bit mux8bit_1 (.A(byteadder_1_sum), .B({8{1'b0}}), .S(and_1_out), .Y(mux8bit_1_y));
  and and_3 (and_3_out, and_2_out, equal8bit_2_eq);
  or or_2 (or_2_out, MATCH, and_3_out);
  and and_4 (and_4_out, or_2_out, not_2_out);
endmodule

module DoorSafety (
  input  CLK,
  input  RESET,
  input  START,
  input  DOOR,
  input  [1:0] MODE,
  input  MOTOR,
  input  ACK,
  output ACK_OK,
  output ACTUAL,
  output ACCEPT,
  output TRIP,
  output [1:0] SNAP
);

  wire and_1_out, and_2_out, and_3_out, and_5_out, and_6_out, and_7_out, and_8_out, and_9_out, and_11_out,
       and_12_out, not_1_out, not_2_out, not_3_out, not_4_out, not_5_out, not_6_out, not_7_out, or_1_out,
       or_2_out, or_3_out, or_4_out, STATE_PENDING_q, STATE_START_PREV_q;

  Register #(.width(1)) STATE_START_PREV (.D(START), .en(1'b1), .Q(STATE_START_PREV_q), .clk(CLK), .clr(RESET));
  Register #(.width(1)) STATE_PENDING (.D(and_12_out), .en(1'b1), .Q(STATE_PENDING_q), .clk(CLK), .clr(RESET));
  Register #(.width(1)) STATE_TRIP (.D(or_4_out), .en(1'b1), .Q(TRIP), .clk(CLK), .clr(RESET));
  Register #(.width(2)) STATE_MODE_SNAPSHOT (.D(MODE), .en(ACCEPT), .Q(SNAP), .clk(CLK), .clr(RESET));
  Register #(.width(1)) STATE_ACK_SUCCESS (.D(ACCEPT), .en(ACK), .Q(ACK_OK), .clk(CLK), .clr(RESET));
  not not_1 (not_1_out, STATE_START_PREV_q);
  not not_2 (not_2_out, TRIP);
  not not_3 (not_3_out, DOOR);
  and and_1 (and_1_out, ACK, START);
  and and_2 (and_2_out, MOTOR, DOOR);
  not not_4 (not_4_out, MOTOR);
  not not_5 (not_5_out, MOTOR);
  and and_3 (and_3_out, START, not_1_out);
  and and_4 (ACTUAL, and_2_out, not_2_out);
  and and_5 (and_5_out, and_1_out, DOOR);
  and and_6 (and_6_out, MOTOR, not_3_out);
  and and_7 (and_7_out, and_3_out, DOOR);
  and and_8 (and_8_out, and_5_out, not_5_out);
  and and_9 (and_9_out, and_7_out, not_4_out);
  or or_1 (or_1_out, STATE_PENDING_q, and_9_out);
  or or_2 (or_2_out, STATE_PENDING_q, and_9_out);
  and and_10 (ACCEPT, and_8_out, or_1_out);
  not not_6 (not_6_out, ACCEPT);
  or or_3 (or_3_out, ACCEPT, and_6_out);
  and and_11 (and_11_out, TRIP, not_6_out);
  not not_7 (not_7_out, or_3_out);
  and and_12 (and_12_out, or_2_out, not_7_out);
  or or_4 (or_4_out, and_6_out, and_11_out);
endmodule

module MemoryAndIO (
  input  CLK,
  input  [7:0] TEMP,
  input  RESET,
  input  [7:0] RPM,
  input  [7:0] ADDRESS,
  input  [7:0] STORE_DATA,
  input  STORE,
  input  START,
  input  DOOR,
  input  [1:0] MODE,
  input  [7:0] WATER,
  output [7:0] READ_DATA,
  output [7:0] COUNT,
  output ACTUAL_MOTOR,
  output MATCH,
  output [7:0] DISPLAY,
  output TRIP,
  output ACCEPT,
  output [1:0] SNAP,
  output [7:0] ACTUATORS
);

  wire and_2_out, and_8_out, and_11_out, and_14_out, and_18_out, and_19_out, and_21_out, and_23_out,
       equal8bit_3_eq, not_1_out;
  wire [0:0] doorsafety_1_ack_ok, timer_1_enable;
  wire [7:0] and_1_out, and_3_out, and_4_out, and_5_out, and_6_out, and_13_out, and_16_out, and_24_out,
       and_25_out, and_26_out, and_27_out, and_28_out, and_29_out, and_30_out, DATA_RAM_dout, or_1_out,
       or_2_out, or_3_out, or_4_out, or_5_out, or_6_out, or_7_out, or_8_out, or_9_out, or_10_out, or_11_out,
       timer_1_limit;
  wire [7:7] equal8bit_1_eq, equal8bit_2_eq, equal8bit_4_eq, equal8bit_5_eq, equal8bit_6_eq, equal8bit_7_eq,
       equal8bit_8_eq, equal8bit_9_eq, equal8bit_10_eq, equal8bit_11_eq, equal8bit_12_eq, equal8bit_13_eq,
       not_2_out;

  Register #(.width(8)) STATE_ACTUATORS (.D(and_1_out), .en(and_18_out), .Q(ACTUATORS), .clk(CLK), .clr(RESET));
  Register #(.width(8)) STATE_DISPLAY (.D(STORE_DATA), .en(and_19_out), .Q(DISPLAY), .clk(CLK), .clr(RESET));
  Equal8Bit equal8bit_1 (.A(ADDRESS), .B(8'hf8), .EQ(equal8bit_1_eq[7]));
  not not_1 (not_1_out, RESET);
  Equal8Bit equal8bit_2 (.A(ADDRESS), .B(8'hf9), .EQ(equal8bit_2_eq[7]));
  Equal8Bit equal8bit_3 (.A(ADDRESS), .B(8'hfa), .EQ(equal8bit_3_eq));
  Equal8Bit equal8bit_4 (.A(ADDRESS), .B(8'hf0), .EQ(equal8bit_4_eq[7]));
  Equal8Bit equal8bit_5 (.A(ADDRESS), .B(8'hfb), .EQ(equal8bit_5_eq[7]));
  Equal8Bit equal8bit_6 (.A(ADDRESS), .B(8'hf1), .EQ(equal8bit_6_eq[7]));
  Equal8Bit equal8bit_7 (.A(ADDRESS), .B(8'hfc), .EQ(equal8bit_7_eq[7]));
  Equal8Bit equal8bit_8 (.A(ADDRESS), .B(8'hf2), .EQ(equal8bit_8_eq[7]));
  Equal8Bit equal8bit_9 (.A(ADDRESS), .B(8'hf3), .EQ(equal8bit_9_eq[7]));
  Equal8Bit equal8bit_10 (.A(ADDRESS), .B(8'hf4), .EQ(equal8bit_10_eq[7]));
  Equal8Bit equal8bit_11 (.A(ADDRESS), .B(8'hf5), .EQ(equal8bit_11_eq[7]));
  Equal8Bit equal8bit_12 (.A(ADDRESS), .B(8'hf6), .EQ(equal8bit_12_eq[7]));
  assign and_1_out = STORE_DATA & 8'h7f;  // AND_Gate and_1, 8 bits wide
  Equal8Bit equal8bit_13 (.A(ADDRESS), .B(8'hf7), .EQ(equal8bit_13_eq[7]));
  and and_2 (and_2_out, STORE, not_1_out);
  not not_2 (not_2_out[7], ADDRESS[7]);
  assign and_3_out = RPM & {8{equal8bit_9_eq[7]}};  // AND_Gate and_3, 8 bits wide
  assign and_4_out = TEMP & {8{equal8bit_8_eq[7]}};  // AND_Gate and_4, 8 bits wide
  assign and_5_out = {4'b0000, MODE, DOOR, START} & {8{equal8bit_4_eq[7]}};  // AND_Gate and_5, 8 bits wide
  assign and_6_out = ACTUATORS & {8{equal8bit_10_eq[7]}};  // AND_Gate and_6, 8 bits wide
  // AND_Gate and_7 has open pins: in0=and_2_out, in1=equal8bit_12_eq[7], out=open
  and and_8 (and_8_out, and_2_out, equal8bit_1_eq[7]);
  // AND_Gate and_9 has open pins: in0=and_2_out, in1=equal8bit_7_eq[7], out=open
  // AND_Gate and_10 has open pins: in0=and_2_out, in1=equal8bit_8_eq[7], out=open
  and and_11 (and_11_out, and_2_out, equal8bit_13_eq[7]);
  // AND_Gate and_12 has open pins: in0=and_2_out, in1=equal8bit_2_eq[7], out=open
  assign and_13_out = WATER & {8{equal8bit_6_eq[7]}};  // AND_Gate and_13, 8 bits wide
  and and_14 (and_14_out, and_2_out, equal8bit_3_eq);
  // AND_Gate and_15 has open pins: in0=and_2_out, in1=equal8bit_9_eq[7], out=open
  assign and_16_out = DISPLAY & {8{equal8bit_11_eq[7]}};  // AND_Gate and_16, 8 bits wide
  // AND_Gate and_17 has open pins: in0=and_2_out, in1=equal8bit_4_eq[7], out=open
  and and_18 (and_18_out, and_2_out, equal8bit_10_eq[7]);
  and and_19 (and_19_out, and_2_out, equal8bit_11_eq[7]);
  // AND_Gate and_20 has open pins: in0=and_2_out, in1=equal8bit_5_eq[7], out=open
  and and_21 (and_21_out, and_2_out, not_2_out[7]);
  // AND_Gate and_22 has open pins: in0=and_2_out, in1=equal8bit_6_eq[7], out=open
  and and_23 (and_23_out, and_14_out, STORE_DATA[0]);
  RAM #(.addrWidth(7), .dataWidth(8), .asyncread("true"), .databus("bibus")) DATA_RAM (
    .addr(ADDRESS[6:0]), .we(and_21_out), .oe(1'b1), .clk(CLK), .din(STORE_DATA), .dout(DATA_RAM_dout));
  Timer timer_1 (
    .CLK(CLK), .RESET(RESET), .DATA(STORE_DATA), .W_LIMIT(and_11_out), .W_CTRL(and_8_out), .COUNT(COUNT),
    .LIMIT(timer_1_limit), .ENABLE(timer_1_enable[0]), .MATCH(MATCH));
  assign and_24_out = DATA_RAM_dout & {8{not_2_out[7]}};  // AND_Gate and_24, 8 bits wide
  assign and_25_out = COUNT & {8{equal8bit_12_eq[7]}};  // AND_Gate and_25, 8 bits wide
  DoorSafety doorsafety_1 (
    .CLK(CLK), .RESET(RESET), .START(START), .DOOR(DOOR), .MODE(MODE), .MOTOR(ACTUATORS[2]),
    .ACK(and_23_out), .ACTUAL(ACTUAL_MOTOR), .TRIP(TRIP), .SNAP(SNAP), .ACK_OK(doorsafety_1_ack_ok[0]),
    .ACCEPT(ACCEPT));
  assign and_26_out = timer_1_limit & {8{equal8bit_13_eq[7]}};  // AND_Gate and_26, 8 bits wide
  assign or_1_out = and_24_out | and_5_out;  // OR_Gate or_1, 8 bits wide
  assign and_27_out = {{7{1'b0}}, timer_1_enable[0]} & {8{equal8bit_1_eq[7]}};  // AND_Gate and_27, 8 bits wide
  assign and_28_out = {{7{1'b0}}, MATCH} & {8{equal8bit_2_eq[7]}};  // AND_Gate and_28, 8 bits wide
  assign or_2_out = or_1_out | and_13_out;  // OR_Gate or_2, 8 bits wide
  assign and_29_out = {{6{1'b0}}, TRIP, doorsafety_1_ack_ok[0]} & {8{equal8bit_7_eq[7]}};  // AND_Gate and_29, 8 bits wide
  assign or_3_out = or_2_out | and_4_out;  // OR_Gate or_3, 8 bits wide
  assign and_30_out = {{6{1'b0}}, SNAP} & {8{equal8bit_5_eq[7]}};  // AND_Gate and_30, 8 bits wide
  assign or_4_out = or_3_out | and_3_out;  // OR_Gate or_4, 8 bits wide
  assign or_5_out = or_4_out | and_6_out;  // OR_Gate or_5, 8 bits wide
  assign or_6_out = or_5_out | and_16_out;  // OR_Gate or_6, 8 bits wide
  assign or_7_out = or_6_out | and_25_out;  // OR_Gate or_7, 8 bits wide
  assign or_8_out = or_7_out | and_26_out;  // OR_Gate or_8, 8 bits wide
  assign or_9_out = or_8_out | and_27_out;  // OR_Gate or_9, 8 bits wide
  assign or_10_out = or_9_out | and_28_out;  // OR_Gate or_10, 8 bits wide
  assign or_11_out = or_10_out | and_30_out;  // OR_Gate or_11, 8 bits wide
  assign READ_DATA = or_11_out | and_29_out;  // OR_Gate or_12, 8 bits wide
endmodule

module Processor (
  input  CLK,
  input  RESET,
  input  [15:0] INSTRUCTION,
  input  [7:0] READ_DATA,
  output [7:0] ADDRESS,
  output STORE,
  output WB_WRITE,
  output FLUSH,
  output [7:0] ID_PC,
  output HALTED,
  output [1:0] FWD_A,
  output [2:0] WB_RD,
  output [7:0] EX_PC,
  output [7:0] MEM_PC,
  output STALL,
  output [1:0] FWD_B,
  output [7:0] WB_PC,
  output [7:0] STORE_DATA,
  output [7:0] PC,
  output [7:0] WB_DATA,
  output [3:0] VALIDS
);

  wire and_1_out, and_2_out, and_3_out, and_4_out, and_5_out, and_7_out, and_9_out, and_10_out, and_11_out,
       and_13_out, and_14_out, and_15_out, equal3bit_1_eq, equal3bit_2_eq, equal8bit_1_eq,
       instructiondecoder_1_bn, instructiondecoder_1_bz, instructiondecoder_1_ht, instructiondecoder_1_jp,
       instructiondecoder_1_ld, instructiondecoder_1_rw, instructiondecoder_1_st, instructiondecoder_1_ud,
       instructiondecoder_1_us, not_1_out, not_2_out, not_3_out, not_4_out, not_5_out, not_6_out, not_7_out,
       or_1_out, or_2_out, or_3_out, or_4_out, or_5_out, or_6_out, or_8_out, or_9_out, or_10_out, or_11_out,
       or_12_out, STATE_EXMEM_LD_q, STATE_EXMEM_RW_q, STATE_EXMEM_ST_q, STATE_IDEX_BN_q, STATE_IDEX_BZ_q,
       STATE_IDEX_HT_q, STATE_IDEX_JP_q, STATE_IDEX_LD_q, STATE_IDEX_RW_q, STATE_IDEX_ST_q, STATE_IDEX_UD_q,
       STATE_IDEX_US_q, STATE_MEMWB_RW_q;
  wire [2:0] instructiondecoder_1_rd, instructiondecoder_1_rs, STATE_EXMEM_RD_q, STATE_IDEX_RD_q,
       STATE_IDEX_RS_q;
  wire [3:0] instructiondecoder_1_op, STATE_IDEX_OP_q;
  wire [7:0] alu_1_result, byteadder_1_sum, forwarding_1_value, forwarding_2_value, instructiondecoder_1_imm,
       mux8bit_1_y, mux8bit_2_y, registerbank_1_a, registerbank_1_b, STATE_IDEX_A_q, STATE_IDEX_B_q,
       STATE_IDEX_IMM_q;
  wire [15:0] STATE_IFID_IR_q;

  Register #(.width(8)) STATE_PC (.D(mux8bit_2_y), .en(or_8_out), .Q(PC), .clk(CLK), .clr(RESET));
  Register #(.width(1)) STATE_HALTED (.D(or_1_out), .en(1'b1), .Q(HALTED), .clk(CLK), .clr(RESET));
  Register #(.width(1)) STATE_IFID_VALID (.D(not_6_out), .en(or_9_out), .Q(VALIDS[0]), .clk(CLK), .clr(RESET));
  Register #(.width(16)) STATE_IFID_IR (.D(INSTRUCTION), .en(or_9_out), .Q(STATE_IFID_IR_q), .clk(CLK), .clr(RESET));
  Register #(.width(8)) STATE_IFID_PC (.D(PC), .en(or_9_out), .Q(ID_PC), .clk(CLK), .clr(RESET));
  Register #(.width(1)) STATE_IDEX_VALID (.D(and_15_out), .en(1'b1), .Q(VALIDS[1]), .clk(CLK), .clr(RESET));
  Register #(.width(8)) STATE_IDEX_PC (.D(ID_PC), .en(1'b1), .Q(EX_PC), .clk(CLK), .clr(RESET));
  Register #(.width(3)) STATE_IDEX_RD (
    .D(instructiondecoder_1_rd), .en(1'b1), .Q(STATE_IDEX_RD_q), .clk(CLK), .clr(RESET));
  Register #(.width(3)) STATE_IDEX_RS (
    .D(instructiondecoder_1_rs), .en(1'b1), .Q(STATE_IDEX_RS_q), .clk(CLK), .clr(RESET));
  Register #(.width(8)) STATE_IDEX_IMM (
    .D(instructiondecoder_1_imm), .en(1'b1), .Q(STATE_IDEX_IMM_q), .clk(CLK), .clr(RESET));
  Register #(.width(4)) STATE_IDEX_OP (
    .D(instructiondecoder_1_op), .en(1'b1), .Q(STATE_IDEX_OP_q), .clk(CLK), .clr(RESET));
  Register #(.width(8)) STATE_IDEX_A (.D(registerbank_1_a), .en(1'b1), .Q(STATE_IDEX_A_q), .clk(CLK), .clr(RESET));
  Register #(.width(8)) STATE_IDEX_B (.D(registerbank_1_b), .en(1'b1), .Q(STATE_IDEX_B_q), .clk(CLK), .clr(RESET));
  Register #(.width(1)) STATE_IDEX_RW (
    .D(instructiondecoder_1_rw), .en(1'b1), .Q(STATE_IDEX_RW_q), .clk(CLK), .clr(RESET));
  Register #(.width(1)) STATE_IDEX_LD (
    .D(instructiondecoder_1_ld), .en(1'b1), .Q(STATE_IDEX_LD_q), .clk(CLK), .clr(RESET));
  Register #(.width(1)) STATE_IDEX_ST (
    .D(instructiondecoder_1_st), .en(1'b1), .Q(STATE_IDEX_ST_q), .clk(CLK), .clr(RESET));
  Register #(.width(1)) STATE_IDEX_UD (
    .D(instructiondecoder_1_ud), .en(1'b1), .Q(STATE_IDEX_UD_q), .clk(CLK), .clr(RESET));
  Register #(.width(1)) STATE_IDEX_US (
    .D(instructiondecoder_1_us), .en(1'b1), .Q(STATE_IDEX_US_q), .clk(CLK), .clr(RESET));
  Register #(.width(1)) STATE_IDEX_BZ (
    .D(instructiondecoder_1_bz), .en(1'b1), .Q(STATE_IDEX_BZ_q), .clk(CLK), .clr(RESET));
  Register #(.width(1)) STATE_IDEX_BN (
    .D(instructiondecoder_1_bn), .en(1'b1), .Q(STATE_IDEX_BN_q), .clk(CLK), .clr(RESET));
  Register #(.width(1)) STATE_IDEX_JP (
    .D(instructiondecoder_1_jp), .en(1'b1), .Q(STATE_IDEX_JP_q), .clk(CLK), .clr(RESET));
  Register #(.width(1)) STATE_IDEX_HT (
    .D(instructiondecoder_1_ht), .en(1'b1), .Q(STATE_IDEX_HT_q), .clk(CLK), .clr(RESET));
  Register #(.width(1)) STATE_EXMEM_VALID (.D(VALIDS[1]), .en(1'b1), .Q(VALIDS[2]), .clk(CLK), .clr(RESET));
  Register #(.width(8)) STATE_EXMEM_PC (.D(EX_PC), .en(1'b1), .Q(MEM_PC), .clk(CLK), .clr(RESET));
  Register #(.width(3)) STATE_EXMEM_RD (.D(STATE_IDEX_RD_q), .en(1'b1), .Q(STATE_EXMEM_RD_q), .clk(CLK), .clr(RESET));
  Register #(.width(8)) STATE_EXMEM_RESULT (.D(alu_1_result), .en(1'b1), .Q(ADDRESS), .clk(CLK), .clr(RESET));
  Register #(.width(8)) STATE_EXMEM_DATA (.D(forwarding_1_value), .en(1'b1), .Q(STORE_DATA), .clk(CLK), .clr(RESET));
  Register #(.width(1)) STATE_EXMEM_RW (.D(STATE_IDEX_RW_q), .en(1'b1), .Q(STATE_EXMEM_RW_q), .clk(CLK), .clr(RESET));
  Register #(.width(1)) STATE_EXMEM_LD (.D(STATE_IDEX_LD_q), .en(1'b1), .Q(STATE_EXMEM_LD_q), .clk(CLK), .clr(RESET));
  Register #(.width(1)) STATE_EXMEM_ST (.D(STATE_IDEX_ST_q), .en(1'b1), .Q(STATE_EXMEM_ST_q), .clk(CLK), .clr(RESET));
  Register #(.width(1)) STATE_MEMWB_VALID (.D(VALIDS[2]), .en(1'b1), .Q(VALIDS[3]), .clk(CLK), .clr(RESET));
  Register #(.width(8)) STATE_MEMWB_PC (.D(MEM_PC), .en(1'b1), .Q(WB_PC), .clk(CLK), .clr(RESET));
  Register #(.width(3)) STATE_MEMWB_RD (.D(STATE_EXMEM_RD_q), .en(1'b1), .Q(WB_RD), .clk(CLK), .clr(RESET));
  Register #(.width(8)) STATE_MEMWB_DATA (.D(mux8bit_1_y), .en(1'b1), .Q(WB_DATA), .clk(CLK), .clr(RESET));
  Register #(.width(1)) STATE_MEMWB_RW (.D(STATE_EXMEM_RW_q), .en(1'b1), .Q(STATE_MEMWB_RW_q), .clk(CLK), .clr(RESET));
  not not_1 (not_1_out, RESET);
  not not_2 (not_2_out, RESET);
  Mux8Bit mux8bit_1 (.A(ADDRESS), .B(READ_DATA), .S(STATE_EXMEM_LD_q), .Y(mux8bit_1_y));
  and and_1 (and_1_out, VALIDS[1], STATE_IDEX_HT_q);
  and and_2 (and_2_out, VALIDS[1], STATE_IDEX_LD_q);
  and and_3 (and_3_out, VALIDS[2], STATE_EXMEM_RW_q);
  ByteAdder byteadder_1 (.A(PC), .B(8'h1), .CIN(1'b0), .SUM(byteadder_1_sum));  // open: COUT
  and and_4 (and_4_out, VALIDS[3], STATE_MEMWB_RW_q);
  and and_5 (and_5_out, VALIDS[2], STATE_EXMEM_ST_q);
  InstructionDecoder instructiondecoder_1 (
    .IR(STATE_IFID_IR_q), .RD(instructiondecoder_1_rd), .RS(instructiondecoder_1_rs),
    .IMM(instructiondecoder_1_imm), .OP(instructiondecoder_1_op), .RW(instructiondecoder_1_rw),
    .LD(instructiondecoder_1_ld), .ST(instructiondecoder_1_st), .UD(instructiondecoder_1_ud),
    .US(instructiondecoder_1_us), .BZ(instructiondecoder_1_bz), .BN(instructiondecoder_1_bn),
    .JP(instructiondecoder_1_jp), .HT(instructiondecoder_1_ht));
  and and_6 (STORE, and_5_out, not_2_out);
  or or_1 (or_1_out, HALTED, and_1_out);
  and and_7 (and_7_out, and_2_out, VALIDS[0]);
  Equal3Bit equal3bit_1 (.A(STATE_IDEX_RD_q), .B(instructiondecoder_1_rd), .EQ(equal3bit_1_eq));
  Equal3Bit equal3bit_2 (.A(STATE_IDEX_RD_q), .B(instructiondecoder_1_rs), .EQ(equal3bit_2_eq));
  and and_8 (WB_WRITE, and_4_out, not_1_out);
  RegisterBank registerbank_1 (
    .CLK(CLK), .RESET(RESET), .WA(WB_RD), .WD(WB_DATA), .WE(WB_WRITE), .RA(instructiondecoder_1_rd),
    .RB(instructiondecoder_1_rs), .A(registerbank_1_a), .B(registerbank_1_b));
  Forwarding forwarding_1 (
    .RAW(STATE_IDEX_A_q), .SRC(STATE_IDEX_RD_q), .USED(STATE_IDEX_UD_q), .EM_RD(STATE_EXMEM_RD_q),
    .EM_W(and_3_out), .EM_LD(STATE_EXMEM_LD_q), .EM_DATA(ADDRESS), .WB_RD(WB_RD), .WB_W(WB_WRITE),
    .WB_DATA(WB_DATA), .VALUE(forwarding_1_value), .SELECT(FWD_A));
  Forwarding forwarding_2 (
    .RAW(STATE_IDEX_B_q), .SRC(STATE_IDEX_RS_q), .USED(STATE_IDEX_US_q), .EM_RD(STATE_EXMEM_RD_q),
    .EM_W(and_3_out), .EM_LD(STATE_EXMEM_LD_q), .EM_DATA(ADDRESS), .WB_RD(WB_RD), .WB_W(WB_WRITE),
    .WB_DATA(WB_DATA), .VALUE(forwarding_2_value), .SELECT(FWD_B));
  and and_9 (and_9_out, instructiondecoder_1_ud, equal3bit_1_eq);
  and and_10 (and_10_out, instructiondecoder_1_us, equal3bit_2_eq);
  Equal8Bit equal8bit_1 (.A(forwarding_1_value), .B({8{1'b0}}), .EQ(equal8bit_1_eq));
  ALU alu_1 (
    .A(forwarding_1_value), .B(forwarding_2_value), .IMM(STATE_IDEX_IMM_q), .OP(STATE_IDEX_OP_q),
    .RESULT(alu_1_result));
  or or_2 (or_2_out, and_9_out, and_10_out);
  not not_3 (not_3_out, equal8bit_1_eq);
  and and_11 (and_11_out, STATE_IDEX_BZ_q, equal8bit_1_eq);
  and and_12 (STALL, and_7_out, or_2_out);
  and and_13 (and_13_out, STATE_IDEX_BN_q, not_3_out);
  or or_3 (or_3_out, STATE_IDEX_JP_q, and_11_out);
  or or_4 (or_4_out, STALL, HALTED);
  or or_5 (or_5_out, or_3_out, and_13_out);
  or or_6 (or_6_out, or_4_out, and_1_out);
  not not_4 (not_4_out, or_4_out);
  and and_14 (and_14_out, VALIDS[1], or_5_out);
  not not_5 (not_5_out, or_6_out);
  or or_7 (FLUSH, and_14_out, and_1_out);
  or or_8 (or_8_out, and_14_out, not_5_out);
  Mux8Bit mux8bit_2 (.A(byteadder_1_sum), .B(STATE_IDEX_IMM_q), .S(and_14_out), .Y(mux8bit_2_y));
  or or_9 (or_9_out, FLUSH, not_4_out);
  or or_10 (or_10_out, FLUSH, STALL);
  or or_11 (or_11_out, HALTED, FLUSH);
  not not_6 (not_6_out, or_11_out);
  or or_12 (or_12_out, or_10_out, HALTED);
  not not_7 (not_7_out, or_12_out);
  and and_15 (and_15_out, VALIDS[0], not_7_out);
endmodule

module WashController (
  input  CLK,
  input  [7:0] DRUM_RPM,
  input  RESET,
  input  START,
  input  [1:0] MODE,
  input  DOOR_CLOSED,
  input  [7:0] WATER_LEVEL,
  input  [7:0] TEMP,
  output [7:0] ID_PC,
  output [2:0] WB_RD,
  output [7:0] ACTUATORS,
  output [1:0] SNAP,
  output VALVE_IN,
  output [7:0] EX_PC,
  output [7:0] WB_DATA,
  output [7:0] DISPLAY,
  output HEATER,
  output [7:0] PC,
  output [7:0] MEM_PC,
  output [7:0] ADDRESS,
  output ACTUAL_MOTOR,
  output CPU_MOTOR_EN,
  output HALTED,
  output [7:0] WB_PC,
  output [7:0] STORE_DATA,
  output TRIP,
  output MOTOR_DIR,
  output STALL,
  output [1:0] FWD_A,
  output STORE,
  output [7:0] COUNT,
  output PUMP_OUT,
  output FLUSH,
  output [1:0] FWD_B,
  output MATCH,
  output DOOR_LOCK,
  output [3:0] VALIDS,
  output WB_WRITE,
  output ACCEPT,
  output BUZZER
);

  wire [7:0] memoryandio_1_read_data;
  wire [15:0] PROGRAM_ROM_data;

  Processor processor_1 (
    .CLK(CLK), .RESET(RESET), .INSTRUCTION(PROGRAM_ROM_data), .READ_DATA(memoryandio_1_read_data), .PC(PC),
    .ADDRESS(ADDRESS), .STORE_DATA(STORE_DATA), .STORE(STORE), .HALTED(HALTED), .STALL(STALL), .FLUSH(FLUSH),
    .VALIDS(VALIDS), .ID_PC(ID_PC), .EX_PC(EX_PC), .MEM_PC(MEM_PC), .WB_PC(WB_PC), .FWD_A(FWD_A),
    .FWD_B(FWD_B), .WB_WRITE(WB_WRITE), .WB_RD(WB_RD), .WB_DATA(WB_DATA));
  ROM #(.addrWidth(8), .dataWidth(16)) PROGRAM_ROM (.addr(PC), .data(PROGRAM_ROM_data));
  MemoryAndIO memoryandio_1 (
    .CLK(CLK), .RESET(RESET), .ADDRESS(ADDRESS), .STORE_DATA(STORE_DATA), .STORE(STORE), .START(START),
    .DOOR(DOOR_CLOSED), .MODE(MODE), .WATER(WATER_LEVEL), .TEMP(TEMP), .RPM(DRUM_RPM),
    .READ_DATA(memoryandio_1_read_data), .ACTUATORS(ACTUATORS), .DISPLAY(DISPLAY),
    .ACTUAL_MOTOR(ACTUAL_MOTOR), .TRIP(TRIP), .COUNT(COUNT), .MATCH(MATCH), .ACCEPT(ACCEPT), .SNAP(SNAP));

  assign BUZZER = ACTUATORS[6];
  assign CPU_MOTOR_EN = ACTUATORS[2];
  assign DOOR_LOCK = ACTUATORS[5];
  assign HEATER = ACTUATORS[1];
  assign MOTOR_DIR = ACTUATORS[3];
  assign PUMP_OUT = ACTUATORS[4];
  assign VALVE_IN = ACTUATORS[0];

  // Notes on the sheet:
  //   contents of PROGRAM_ROM (hex, n*v repeats v):
  //   1e03 1a02 1cf0 6180 51c0 41c0 a002 1cfa 1001 7180 1cfc 6180 1201 5040 9002 1cfb 6180 a016 1464 1650
  //   1828 b019 1496 1678 183c 1cf4 1021 7180 1cf5 1001 7180 1cf1 6180 d080 901f 1cf4 1020 7180 1cf7 7780
  //   1cf8 1003 7180 1224 1cf4 7380 1cfc 6180 5140 a069 1cf9 6180 a03c 1024 4040 903a 1224 b02c 122c b02c
  //   1cf4 1030 7180 1cf8 1000 7180 1cf5 1002 7180 1cf1 6180 120a d200 9245 1cf4 1020 7180 1cf7 7980 1cf8
  //   1003 7180 1cf4 1024 7180 1cfc 6180 5140 a069 1cf9 6180 9055 1cf4 1020 7180 1cf8 1000 7180 1cf5 10aa
  //   7180 1cf4 1040 7180 c000 1cf4 1000 7180 1cf8 7180 1cf5 10ee 7180 b002 0000 0000 0000 0000 0000 0000
  //   0000 0000 0000 0000 0000 0000 0000 0000 0000 0000 0000 0000 0000 0000 0000 0000 0000 0000 0000 0000
  //   0000 0000 0000 0000 0000 0000 0000 0000 0000 0000 0000 0000 0000 0000 0000 0000 0000 0000 0000 0000
  //   0000 0000 0000 0000 0000 0000 0000 0000 0000 0000 0000 0000 0000 0000 0000 0000 0000 0000 0000 0000
  //   0000 0000 0000 0000 0000 0000 0000 0000 0000 0000 0000 0000 0000 0000 0000 0000 0000 0000 0000 0000
  //   0000 0000 0000 0000 0000 0000 0000 0000 0000 0000 0000 0000 0000 0000 0000 0000 0000 0000 0000 0000
  //   0000 0000 0000 0000 0000 0000 0000 0000 0000 0000 0000 0000 0000 0000 0000 0000 0000 0000 0000 0000
  //   0000 0000 0000 0000 0000 0000 0000 0000 0000 0000 0000 0000 0000 0000 0000 0000
endmodule

module Main (
  input  RESET,
  input  START,
  input  [1:0] MODE,
  input  DOOR_CLOSED,
  input  [7:0] WATER_LEVEL,
  input  [7:0] TEMP,
  input  [7:0] DRUM_RPM,
  output [7:0] PC,
  output HALTED,
  output STALL,
  output FLUSH,
  output [3:0] VALIDS,
  output [7:0] ID_PC,
  output [7:0] EX_PC,
  output [7:0] MEM_PC,
  output [7:0] WB_PC,
  output [1:0] FWD_A,
  output [1:0] FWD_B,
  output WB_WRITE,
  output [2:0] WB_RD,
  output [7:0] WB_DATA,
  output [7:0] ADDRESS,
  output [7:0] STORE_DATA,
  output STORE,
  output [7:0] ACTUATORS,
  output [7:0] DISPLAY,
  output ACTUAL_MOTOR,
  output TRIP,
  output [7:0] COUNT,
  output MATCH,
  output ACCEPT,
  output [1:0] SNAP,
  output VALVE_IN,
  output HEATER,
  output CPU_MOTOR_EN,
  output MOTOR_DIR,
  output PUMP_OUT,
  output DOOR_LOCK,
  output BUZZER
);

  wire GLOBAL_CLOCK_out;

  Clock #(.highDuration(1), .lowDuration(1)) GLOBAL_CLOCK (.out(GLOBAL_CLOCK_out));
  WashController washcontroller_1 (
    .CLK(GLOBAL_CLOCK_out), .RESET(RESET), .START(START), .MODE(MODE), .DOOR_CLOSED(DOOR_CLOSED),
    .WATER_LEVEL(WATER_LEVEL), .TEMP(TEMP), .DRUM_RPM(DRUM_RPM), .PC(PC), .HALTED(HALTED), .STALL(STALL),
    .FLUSH(FLUSH), .VALIDS(VALIDS), .ID_PC(ID_PC), .EX_PC(EX_PC), .MEM_PC(MEM_PC), .WB_PC(WB_PC),
    .FWD_A(FWD_A), .FWD_B(FWD_B), .WB_WRITE(WB_WRITE), .WB_RD(WB_RD), .WB_DATA(WB_DATA), .ADDRESS(ADDRESS),
    .STORE_DATA(STORE_DATA), .STORE(STORE), .ACTUATORS(ACTUATORS), .DISPLAY(DISPLAY),
    .ACTUAL_MOTOR(ACTUAL_MOTOR), .TRIP(TRIP), .COUNT(COUNT), .MATCH(MATCH), .ACCEPT(ACCEPT), .SNAP(SNAP),
    .VALVE_IN(VALVE_IN), .HEATER(HEATER), .CPU_MOTOR_EN(CPU_MOTOR_EN), .MOTOR_DIR(MOTOR_DIR),
    .PUMP_OUT(PUMP_OUT), .DOOR_LOCK(DOOR_LOCK), .BUZZER(BUZZER));
endmodule
